// Digital circuit Multiplexer (1 bit, 16x1).dig as structural Verilog
module Multiplexer__1_bit__16x1 (
  input  [15:0] sig,
  input  [3:0] sel,
  output Z
);

  wire and_1_out, and_2_out, multiplexer__1_bit__8x1_1_z, multiplexer__1_bit__8x1_2_z;

  Multiplexer__1_bit__8x1 multiplexer__1_bit__8x1_1 (.sig(sig[7:0]), .sel(sel[2:0]), .Z(multiplexer__1_bit__8x1_1_z));
  Multiplexer__1_bit__8x1 multiplexer__1_bit__8x1_2 (.sig(sig[15:8]), .sel(sel[2:0]), .Z(multiplexer__1_bit__8x1_2_z));
  and and_1 (and_1_out, multiplexer__1_bit__8x1_1_z, ~sel[3]);  // And
  and and_2 (and_2_out, multiplexer__1_bit__8x1_2_z, sel[3]);
  or or_1 (Z, and_1_out, and_2_out);
endmodule
