// Digital circuit Multiplexer (1 bit, 2x1).dig as structural Verilog
module Multiplexer__1_bit__2x1 (
  input  s0,
  input  s1,
  input  sel,
  output S
);

  wire and_1_out, and_2_out;

  and and_1 (and_1_out, s0, ~sel);  // And
  and and_2 (and_2_out, s1, sel);
  or or_1 (S, and_1_out, and_2_out);
endmodule
