// Digital circuit Multiplexer (1 bit, 32x1).dig as structural Verilog
module Multiplexer__1_bit__32x1 (
  input  [31:0] sig,
  input  [4:0] sel,
  output Z
);

  wire and_1_out, and_2_out, multiplexer__1_bit__16x1_1_z, multiplexer__1_bit__16x1_2_z;

  Multiplexer__1_bit__16x1 multiplexer__1_bit__16x1_1 (
    .sig(sig[15:0]), .sel(sel[3:0]), .Z(multiplexer__1_bit__16x1_1_z));
  Multiplexer__1_bit__16x1 multiplexer__1_bit__16x1_2 (
    .sig(sig[31:16]), .sel(sel[3:0]), .Z(multiplexer__1_bit__16x1_2_z));
  and and_1 (and_1_out, multiplexer__1_bit__16x1_1_z, ~sel[4]);  // And
  and and_2 (and_2_out, multiplexer__1_bit__16x1_2_z, sel[4]);
  or or_1 (Z, and_1_out, and_2_out);
endmodule
