// Digital circuit Multiplexer (1 bit, 4x1).dig as structural Verilog
module Multiplexer__1_bit__4x1 (
  input  [3:0] sig,
  input  [1:0] sel,
  output Z
);

  wire and_1_out, and_2_out, multiplexer__1_bit__2x1_1_z, multiplexer__1_bit__2x1_2_z;

  Multiplexer__1_bit__2x1 multiplexer__1_bit__2x1_1 (.sig(sig[1:0]), .sel(sel[0]), .Z(multiplexer__1_bit__2x1_1_z));
  Multiplexer__1_bit__2x1 multiplexer__1_bit__2x1_2 (.sig(sig[3:2]), .sel(sel[0]), .Z(multiplexer__1_bit__2x1_2_z));
  and and_1 (and_1_out, multiplexer__1_bit__2x1_1_z, ~sel[1]);  // And
  and and_2 (and_2_out, multiplexer__1_bit__2x1_2_z, sel[1]);
  or or_1 (Z, and_1_out, and_2_out);
endmodule
